// Logisim project SAP1.circ as structural Verilog: 13 circuits, main circuit main2
module ALU (
  input  [7:0] A,
  input  [7:0] B,
  input  Su,
  input  EU,
  output [7:0] S_out
);

  wire [7:0] adder_1_out, multiplexer_1_out, subtractor_1_out;

  Adder adder_1 (.a(A), .b(B), .out(adder_1_out));  // open: cin, cout
  Subtractor subtractor_1 (.a(A), .b(B), .out(subtractor_1_out));  // open: bin, bout
  Multiplexer #(.width(8)) multiplexer_1 (.in0(adder_1_out), .in1(subtractor_1_out), .out(multiplexer_1_out), .sel(Su));
  assign S_out = EU ? multiplexer_1_out : 8'bz;  // Controlled_Buffer controlled_buffer_1
endmodule

module CU (
  input  CLK,
  input  CLR,
  input  [3:0] OP,
  output CP,
  output EP,
  output LM,
  output CE,
  output LI,
  output EI,
  output LA,
  output EA,
  output SU,
  output EU,
  output LB,
  output LO,
  output HALT
);

  wire and_1_out, and_2_out, and_3_out, and_4_out, and_5_out, and_6_out, and_7_out, and_8_out, and_9_out,
       and_10_out, and_11_out, and_12_out, and_15_out, and_16_out, and_17_out, and_18_out, id_1_add,
       id_1_lda, id_1_oup, id_1_sub, rc_1_t4, rc_1_t5, rc_1_t6;

  RC rc_1 (.CLK(CLK), .CLR(CLR), .T1(EP), .T2(CP), .T3(LI), .T4(rc_1_t4), .T5(rc_1_t5), .T6(rc_1_t6));
  ID id_1 (
    .I7(OP[3]), .I6(OP[2]), .I5(OP[1]), .I4(OP[0]), .LDA(id_1_lda), .ADD(id_1_add), .SUB(id_1_sub),
    .OUP(id_1_oup), .HALT(HALT));
  and and_1 (and_1_out, id_1_lda, rc_1_t4);
  and and_2 (and_2_out, id_1_add, rc_1_t4);
  and and_3 (and_3_out, id_1_sub, rc_1_t4);
  or or_1 (LM, EP, and_1_out, and_2_out, and_3_out);
  and and_4 (and_4_out, id_1_lda, rc_1_t5);
  and and_5 (and_5_out, id_1_add, rc_1_t5);
  and and_6 (and_6_out, id_1_sub, rc_1_t5);
  or or_2 (CE, LI, and_4_out, and_5_out, and_6_out);
  and and_7 (and_7_out, id_1_lda, rc_1_t4);
  and and_8 (and_8_out, id_1_add, rc_1_t4);
  and and_9 (and_9_out, id_1_sub, rc_1_t4);
  or or_3 (EI, and_7_out, and_8_out, and_9_out);
  and and_10 (and_10_out, id_1_lda, rc_1_t5);
  and and_11 (and_11_out, id_1_add, rc_1_t6);
  or or_4 (LA, and_10_out, and_11_out, and_12_out);
  and and_12 (and_12_out, id_1_sub, rc_1_t6);
  and and_13 (EA, id_1_oup, rc_1_t4);
  and and_14 (SU, id_1_sub, rc_1_t6);
  and and_15 (and_15_out, id_1_add, rc_1_t6);
  or or_5 (EU, and_15_out, and_16_out);
  and and_16 (and_16_out, id_1_sub, rc_1_t6);
  and and_17 (and_17_out, id_1_add, rc_1_t5);
  or or_6 (LB, and_17_out, and_18_out);
  and and_18 (and_18_out, id_1_sub, rc_1_t5);
  and and_19 (LO, id_1_oup, rc_1_t4);
endmodule

module MAR (
  input  [3:0] BUS_IN,
  input  LM,
  input  CLK,
  output [3:0] RAM_ADDR
);

  wire and_1_out;

  and and_1 (and_1_out, LM, CLK);
  D_Flip_Flop d_ff_1 (.D(BUS_IN[0]), .clk(and_1_out), .Q(RAM_ADDR[0]));  // open: Qn, preset, reset
  D_Flip_Flop d_ff_2 (.D(BUS_IN[1]), .clk(and_1_out), .Q(RAM_ADDR[1]));  // open: Qn, preset, reset
  D_Flip_Flop d_ff_3 (.D(BUS_IN[2]), .clk(and_1_out), .Q(RAM_ADDR[2]));  // open: Qn, preset, reset
  D_Flip_Flop d_ff_4 (.D(BUS_IN[3]), .clk(and_1_out), .Q(RAM_ADDR[3]));  // open: Qn, preset, reset
endmodule

module PC (
  input  CLK,
  input  CLR,
  input  Cp,
  input  EP,
  output [7:0] out_5
);

  wire and_1_out, j_k_ff_1_q, j_k_ff_2_q, j_k_ff_3_q, j_k_ff_4_q;

  and and_1 (and_1_out, CLK, Cp);
  J_K_Flip_Flop #(.trigger("falling")) j_k_ff_1 (
    .J(1'b1), .K(1'b1), .clk(and_1_out), .Q(j_k_ff_1_q), .reset(CLR));  // open: Qn, preset
  J_K_Flip_Flop #(.trigger("falling")) j_k_ff_2 (
    .J(1'b1), .K(1'b1), .clk(j_k_ff_1_q), .Q(j_k_ff_2_q), .reset(CLR));  // open: Qn, preset
  assign out_5[0] = EP ? j_k_ff_1_q : 1'bz;  // Controlled_Buffer controlled_buffer_1
  J_K_Flip_Flop #(.trigger("falling")) j_k_ff_3 (
    .J(1'b1), .K(1'b1), .clk(j_k_ff_2_q), .Q(j_k_ff_3_q), .reset(CLR));  // open: Qn, preset
  assign out_5[1] = EP ? j_k_ff_2_q : 1'bz;  // Controlled_Buffer controlled_buffer_2
  assign out_5[2] = EP ? j_k_ff_3_q : 1'bz;  // Controlled_Buffer controlled_buffer_3
  J_K_Flip_Flop #(.trigger("falling")) j_k_ff_4 (
    .J(1'b1), .K(1'b1), .clk(j_k_ff_3_q), .Q(j_k_ff_4_q), .reset(CLR));  // open: Qn, preset
  assign out_5[3] = EP ? j_k_ff_4_q : 1'bz;  // Controlled_Buffer controlled_buffer_4
endmodule

module A_REG (
  input  [7:0] BUS_IN,
  input  CLK,
  input  LA,
  input  CLR,
  input  EA,
  output [7:0] ALU_A,
  output [7:0] BUS_OUT
);

  Register register_1 (.D(BUS_IN), .en(LA), .clk(CLK), .Q(ALU_A), .clr(CLR));
  assign BUS_OUT = EA ? ALU_A : 8'bz;  // Controlled_Buffer controlled_buffer_1
endmodule

module B_REG (
  input  [7:0] BUS_IN,
  input  LB,
  input  CLK,
  input  CLR,
  output [7:0] ALU_B
);

  Register register_1 (.D(BUS_IN), .en(LB), .clk(CLK), .Q(ALU_B), .clr(CLR));
endmodule

module OUTPUT_REG (
  input  [7:0] BUS_IN,
  input  LO,
  input  CLK,
  input  CLR,
  output [7:0] CPU_OUT
);

  Register register_1 (.D(BUS_IN), .en(LO), .clk(CLK), .Q(CPU_OUT), .clr(CLR));
endmodule

module IR (
  input  [7:0] BUS_IN,
  input  LI,
  input  CLK,
  input  EI,
  input  CLR,
  output [3:0] CONTROL,
  output [7:0] BUS_OUT
);

  wire and_1_out, and_2_out, d_ff_5_q, d_ff_6_q, d_ff_7_q, d_ff_8_q;

  and and_1 (and_1_out, CLK, LI);
  D_Flip_Flop d_ff_1 (.D(BUS_IN[4]), .clk(and_1_out), .Q(CONTROL[0]));  // open: Qn, preset, reset
  D_Flip_Flop d_ff_2 (.D(BUS_IN[5]), .clk(and_1_out), .Q(CONTROL[1]));  // open: Qn, preset, reset
  D_Flip_Flop d_ff_3 (.D(BUS_IN[6]), .clk(and_1_out), .Q(CONTROL[2]));  // open: Qn, preset, reset
  D_Flip_Flop d_ff_4 (.D(BUS_IN[7]), .clk(and_1_out), .Q(CONTROL[3]), .reset(CLR));  // open: Qn, preset
  and and_2 (and_2_out, CLK, LI);
  D_Flip_Flop d_ff_5 (.D(BUS_IN[0]), .clk(and_2_out), .Q(d_ff_5_q));  // open: Qn, preset, reset
  D_Flip_Flop d_ff_6 (.D(BUS_IN[1]), .clk(and_2_out), .Q(d_ff_6_q));  // open: Qn, preset, reset
  D_Flip_Flop d_ff_7 (.D(BUS_IN[2]), .clk(and_2_out), .Q(d_ff_7_q));  // open: Qn, preset, reset
  D_Flip_Flop d_ff_8 (.D(BUS_IN[3]), .clk(and_2_out), .Q(d_ff_8_q), .reset(CLR));  // open: Qn, preset
  assign BUS_OUT[0] = EI ? d_ff_5_q : 1'bz;  // Controlled_Buffer controlled_buffer_1
  assign BUS_OUT[1] = EI ? d_ff_6_q : 1'bz;  // Controlled_Buffer controlled_buffer_2
  assign BUS_OUT[2] = EI ? d_ff_7_q : 1'bz;  // Controlled_Buffer controlled_buffer_3
  assign BUS_OUT[3] = EI ? d_ff_8_q : 1'bz;  // Controlled_Buffer controlled_buffer_4

  // Other names for the same wires on the sheet: LN[3:0] = BUS_IN[3:0]; UN[3:0] = BUS_IN[7:4]
endmodule

module RC (
  input  CLK,
  input  CLR,
  output T1,
  output T2,
  output T3,
  output T4,
  output T5,
  output T6
);

  wire j_k_ff_1_q, j_k_ff_2_qn, j_k_ff_3_qn, j_k_ff_4_qn, j_k_ff_5_qn, j_k_ff_6_qn;

  J_K_Flip_Flop #(.trigger("falling")) j_k_ff_1 (
    .J(j_k_ff_6_qn), .K(T6), .clk(CLK), .Q(j_k_ff_1_q), .Qn(T1), .reset(CLR));  // open: preset
  J_K_Flip_Flop #(.trigger("falling")) j_k_ff_2 (
    .J(T1), .K(j_k_ff_1_q), .clk(CLK), .Q(T2), .Qn(j_k_ff_2_qn), .reset(CLR));  // open: preset
  J_K_Flip_Flop #(.trigger("falling")) j_k_ff_3 (
    .J(T2), .K(j_k_ff_2_qn), .clk(CLK), .Q(T3), .Qn(j_k_ff_3_qn), .reset(CLR));  // open: preset
  J_K_Flip_Flop #(.trigger("falling")) j_k_ff_4 (
    .J(T3), .K(j_k_ff_3_qn), .clk(CLK), .Q(T4), .Qn(j_k_ff_4_qn), .reset(CLR));  // open: preset
  J_K_Flip_Flop #(.trigger("falling")) j_k_ff_5 (
    .J(T4), .K(j_k_ff_4_qn), .clk(CLK), .Q(T5), .Qn(j_k_ff_5_qn), .reset(CLR));  // open: preset
  J_K_Flip_Flop #(.trigger("falling")) j_k_ff_6 (
    .J(T5), .K(j_k_ff_5_qn), .clk(CLK), .Q(T6), .Qn(j_k_ff_6_qn), .reset(CLR));  // open: preset
endmodule

module ID (
  input  I7,
  input  I6,
  input  I5,
  input  I4,
  output LDA,
  output ADD,
  output SUB,
  output OUP,
  output HALT
);

  wire not_1_out, not_2_out, not_3_out, not_4_out;

  not not_1 (not_1_out, I7);
  not not_2 (not_2_out, I6);
  not not_3 (not_3_out, I5);
  not not_4 (not_4_out, I4);
  and and_1 (LDA, not_1_out, not_2_out, not_3_out, not_4_out);
  and and_2 (ADD, not_1_out, not_2_out, not_3_out, I4);
  and and_3 (SUB, not_1_out, not_2_out, I5, not_4_out);
  and and_4 (OUP, I7, I6, I5, not_4_out);
  and and_5 (HALT, I7, I6, I5, I4);
endmodule

module test (
  input  in_1,
  input  in_2,
  input  [3:0] in_3
);

  wire cu_1_ce, cu_1_cp, cu_1_ea, cu_1_ei, cu_1_ep, cu_1_eu, cu_1_halt, cu_1_la, cu_1_lb, cu_1_li, cu_1_lm,
       cu_1_lo, cu_1_su;

  LED led_1 (.in(cu_1_cp));
  CU cu_1 (
    .CLK(in_1), .CLR(in_2), .OP(in_3), .CP(cu_1_cp), .EP(cu_1_ep), .LM(cu_1_lm), .CE(cu_1_ce), .LI(cu_1_li),
    .EI(cu_1_ei), .LA(cu_1_la), .EA(cu_1_ea), .SU(cu_1_su), .EU(cu_1_eu), .LB(cu_1_lb), .LO(cu_1_lo),
    .HALT(cu_1_halt));
  LED led_2 (.in(cu_1_ep));
  LED led_3 (.in(cu_1_lm));
  LED led_4 (.in(cu_1_ce));
  LED led_5 (.in(cu_1_li));
  LED led_6 (.in(cu_1_ei));
  LED led_7 (.in(cu_1_la));
  LED led_8 (.in(cu_1_ea));
  LED led_9 (.in(cu_1_su));
  LED led_10 (.in(cu_1_eu));
  LED led_11 (.in(cu_1_lb));
  LED led_12 (.in(cu_1_lo));
  LED led_13 (.in(cu_1_halt));
endmodule

module main2 (
  input  in_1,
  input  in_2,
  input  [3:0] in_3,
  input  [7:0] in_4,
  input  in_5,
  output [7:0] out_6
);

  wire bcd_to_7_segment_decoder_2_p1, bcd_to_7_segment_decoder_3_p1, binary_to_bcd_converter_1_p2, Ce, CLK,
       clock_1_out, controller_1_clock_o, controller_1_write_o, Cp, Ea, Ei, Ep, Eu, HALT, La, Lb, Li, Lm, Lo,
       not_1_out, Su;
  wire [3:0] CNTRL, controller_1_addr_o, RAM_ADDR;
  wire [7:0] A, B, controller_1_d_o, CPU_OUT, ram_1_dout;

  RAM #(.addrWidth(4), .enables("line")) ram_1 (
    .addr(controller_1_addr_o), .we(controller_1_write_o), .clk(controller_1_clock_o),
    .din(controller_1_d_o), .dout(ram_1_dout));
  Controller controller_1 (
    .Custom_Data_In(in_4), .Bus_Data_In(out_6), .Custom_Addr_In(in_3), .Bus_Addr_In(RAM_ADDR), .RUN(in_2),
    .WRITE(in_5), .CLOCK(CLK), .ADDR_O(controller_1_addr_o), .D_O(controller_1_d_o),
    .WRITE_O(controller_1_write_o), .CLOCK_O(controller_1_clock_o));  // open: OE
  CU cu_1 (
    .CLK(CLK), .CLR(in_1), .OP(CNTRL), .CP(Cp), .EP(Ep), .LM(Lm), .CE(Ce), .LI(Li), .EI(Ei), .LA(La),
    .EA(Ea), .SU(Su), .EU(Eu), .LB(Lb), .LO(Lo), .HALT(HALT));
  PC pc_1 (.CLK(CLK), .CLR(in_1), .Cp(Cp), .EP(Ep), .out_5(out_6));
  MAR mar_1 (.BUS_IN(out_6[3:0]), .LM(Lm), .CLK(CLK), .RAM_ADDR(RAM_ADDR));
  IR ir_1 (.BUS_IN(out_6), .LI(Li), .CLK(CLK), .EI(Ei), .CLR(in_1), .CONTROL(CNTRL), .BUS_OUT(out_6));
  assign out_6 = Ce ? ram_1_dout : 8'bz;  // Controlled_Buffer controlled_buffer_1
  A_REG a_reg_1 (.BUS_IN(out_6), .CLK(CLK), .LA(La), .CLR(in_1), .EA(Ea), .ALU_A(A), .BUS_OUT(out_6));
  ALU alu_1 (.A(A), .B(B), .Su(Su), .EU(Eu), .S_out(out_6));
  B_REG b_reg_1 (.BUS_IN(out_6), .LB(Lb), .CLK(CLK), .CLR(in_1), .ALU_B(B));
  OUTPUT_REG output_reg_1 (.BUS_IN(out_6), .LO(Lo), .CLK(CLK), .CLR(in_1), .CPU_OUT(CPU_OUT));
  // BCD_to_7_Segment_decoder bcd_to_7_segment_decoder_1: pin names not known
  // BCD_to_7_Segment_decoder bcd_to_7_segment_decoder_2: pin names not known; wires that end beside it: bcd_to_7_segment_decoder_2_p1
  _7_Segment_Display u_7_segment_display_1 ();  // open: g, f, a, b, e, d, c, dp
  _7_Segment_Display u_7_segment_display_2 ();  // open: g, f, a, b, e, d, c, dp
  // Binary_to_BCD_converter #(.binvalue(8)) binary_to_bcd_converter_1: pin names not known; wires that end beside it: CPU_OUT, binary_to_bcd_converter_1_p2, binary_to_bcd_converter_1_p2, bcd_to_7_segment_decoder_2_p1
  J_K_Flip_Flop j_k_ff_1 (.J(not_1_out), .K(not_1_out), .clk(clock_1_out), .Q(CLK));  // open: Qn, preset, reset
  not not_1 (not_1_out, HALT);
  Clock clock_1 (.out(clock_1_out));
  // BCD_to_7_Segment_decoder bcd_to_7_segment_decoder_3: pin names not known; wires that end beside it: bcd_to_7_segment_decoder_3_p1, bcd_to_7_segment_decoder_3_p1
  _7_Segment_Display u_7_segment_display_3 ();  // open: g, f, a, b, e, d, c, dp
  // Digital_Oscilloscope digital_oscilloscope_1: pin names not known; wires that end beside it: CLK, Ep, Cp, Ce, Li, Lm, Ei, La, Ea, Lb, Eu

  // Other names for the same wires on the sheet: CLR = in_1; CUSTOM_ADDR[3:0] = in_3; CUSTOM_DATA[7:0] = in_4;
  //   RUN = in_2; W_BUS[7:0] = out_6; WRITE = in_5

  // Notes on the sheet:
  //   ------------------OPCODE------------------
  //   LDA: 0000
  //   ADD: 0001
  //   SUB: 0010
  //   OUP: 1110
  //   HLT: 1111
endmodule

module Controller (
  input  [7:0] Custom_Data_In,
  input  [7:0] Bus_Data_In,
  input  [3:0] Custom_Addr_In,
  input  [3:0] Bus_Addr_In,
  input  RUN,
  input  WRITE,
  input  CLOCK,
  output [3:0] ADDR_O,
  output [7:0] D_O,
  output WRITE_O,
  output OE,
  output CLOCK_O
);

  Multiplexer #(.width(8)) multiplexer_1 (.in0(Custom_Data_In), .in1(Bus_Data_In), .out(D_O), .sel(RUN));
  Multiplexer #(.width(4)) multiplexer_2 (.in0(Custom_Addr_In), .in1(Bus_Addr_In), .out(ADDR_O), .sel(RUN));
  or or_1 (CLOCK_O, WRITE, CLOCK);

  assign OE = 1'b1;
  assign WRITE_O = WRITE;
endmodule
